# Fritzing sketch 3D_scanner_fritzing (saved by Fritzing 0.9.2b)

parts:
  Part1 = Arduino Uno (Rev3)
  J1 = Basic Servo
  J2 = Basic Servo
  Part2 = LIDAR-Lite
  GY1 = MPU-6050 Board GY-521 [form="♀ (female)" package=THT]

nets:
  N1: Part1.A4/SDA, Part2.SDA, GY1.pin4
  N2: Part1.A5/SCL, Part2.SCL, GY1.pin3
  N3: Part1.D1/TX, GY1.pin8
  N4: Part1.D6_PWM, J2.pulse
  N5: Part1.D7, J1.pulse
  5V: Part1.5V, J2.vcc, Part2.5V, GY1.pin1
  GND: Part1.GND, J1.gnd, J2.gnd, Part2.GND, GY1.pin2

custom parts:
  LIDAR-Lite: PulsedLight LIDAR-Lite Sensor
  MPU-6050 Board GY-521: Acelerometro y Giroscopio MPU-6050 Board GY-521
